# Fritzing sketch Potentiometer1 (saved by Fritzing 0.9.5d)
breadboards: 1

parts:
  パーツ1 = Arduino Uno (Rev3)
  U1 = POT_SWITCH [package=pot_pth_switch]  # not connected
  U2 = POT [package=trim_pot]  # not connected
  R2 = TRIMPOT [package=trimpot-5mm]  # not connected
  R3 = Trimmer Potentiometer [package=THT]

nets:
  N1: パーツ1.A0, R3.wiper
  N2: パーツ1.5V, R3.leg2
  N3: パーツ1.GND, R3.leg1

custom parts:
  Trimmer Potentiometer: A standard adjustable resistor (potentiometer).
