# Fritzing sketch Potentiometer1 (saved by Fritzing 0.9.5d)
breadboards: 1

parts:
  パーツ1 = Arduino Uno (Rev3)
  U1 = POT_SWITCH [package=pot_pth_switch]  # not connected
  U2 = POT [package=trim_pot]  # not connected
  R2 = TRIMPOT [package=trimpot-5mm]  # not connected
  R3 = Trimmer Potentiometer [package=THT]
  LED1 = LED - 5mm [color="Red (633nm)" package="5 mm [THT]"]
  R4 = Resistor [tolerance=±5% resistance=220 package=THT]

nets:
  N1: パーツ1.A0, R3.wiper
  N2: パーツ1.D9_PWM, LED1.anode
  N3: パーツ1.5V, R3.leg2
  N4: パーツ1.GND, R3.leg1, R4.Pin_1
  N5: LED1.cathode, R4.Pin_0

custom parts:
  Trimmer Potentiometer: A standard adjustable resistor (potentiometer).
